// Logisim project CPUDESIGN.circ as structural Verilog
module main (
  input  START,
  input  in_2
);

  wire AC_15, AC_CLR, AC_INR, AC_IS_0, AC_LOAD, and_1_out, and_2_out, and_3_out, and_4_out, and_5_out,
       and_6_out, AR_INR, AR_LOAD, CLK, D0, D1, D2, D3, D4, D5, D6, D7, DR_INR, DR_IS_0, DR_LOAD, E_output,
       I, IR_LOAD, not_1_out, or_1_out, or_2_out, or_3_out, PC_CLR, PC_INR, PC_LOAD, rB0, rB1, rB2, rB3, rB4,
       rB5, rB6, rB7, rB8, rB9, rB10, rB11, READ_EN, SC_CLR, SC_INR, T0, T1, T2, T3, T4, T5, T6, T7, WRITE_EN;
  wire [2:0] ALU_S2S1S0, BUS_S2S1S0;
  wire [15:0] AC_OUTPUT, AR_OUTPUT, DR_OUTPUT, IR_OUTPUT, PC_OUTPUT;

  Clock clock_1 (.out(CLK));
  and and_1 (and_1_out, D1, T5);
  not not_1 (not_1_out, SC_CLR);
  and and_2 (and_2_out, D1, T5);
  or or_1 (or_1_out, SC_CLR, rB0);
  and and_3 (and_3_out, not_1_out, SC_INR);
  or or_2 (or_2_out, rB7, rB6, and_1_out);
  D_Flip_Flop d_ff_1 (.D(or_3_out), .clk(CLK), .Q(SC_INR));  // open: Qn, preset, reset
  or or_3 (or_3_out, START, and_3_out);
  COMMON_BUS common_bus_1 (
    .E_COMP(rB8), .READ_ENABLE(READ_EN), .E_LOAD(or_2_out), .E_CLR(rB10), .WRITE_ENABLE(WRITE_EN),
    .ALU_SELECTION_BITS(ALU_S2S1S0), .CLK(CLK), .CommonBus_Selection(BUS_S2S1S0), .AR_INR(AR_INR),
    .AR_LOAD(AR_LOAD), .AR_CLR(1'b0), .PC_INR(PC_INR), .PC_LOAD(PC_LOAD), .PC_CLR(in_2), .DATA_INR(DR_INR),
    .DATA_LOAD(DR_LOAD), .DATA_CLR(1'b0), .AC_INR(AC_INR), .AC_LOAD(AC_LOAD), .AC_CLR(AC_CLR),
    .IR_LOAD(IR_LOAD), .TR_INR(1'b0), .TR_LOAD(1'b0), .TR_CLR(1'b0), .rB7(rB7), .rB6(rB6), .D1T5(and_2_out),
    .E_output(E_output), .AR_out(AR_OUTPUT), .PC_out(PC_OUTPUT), .DR_15_0(DR_OUTPUT), .AC_15_0(AC_OUTPUT),
    .IR_DATA(IR_OUTPUT));
  INSTRUCTION_REGISTER instruction_register_1 (
    .IR_15_0_BITS(IR_OUTPUT), .SC_INR(SC_INR), .SC_CLR(or_1_out), .SC_CLK(CLK), .Ibit_Control(T2), .CLK(CLK),
    .rB0(rB0), .rB1(rB1), .rB2(rB2), .D0(D0), .D1(D1), .D2(D2), .rB3(rB3), .D3(D3), .rB4(rB4), .rB5(rB5),
    .T0(T0), .D4(D4), .T1(T1), .T2(T2), .D5(D5), .T3(T3), .rB6(rB6), .D6(D6), .D7(D7), .rB7(rB7), .rB8(rB8),
    .T4(T4), .rB9(rB9), .T5(T5), .T6(T6), .rB10(rB10), .T7(T7), .rB11(rB11), .I(I));
  // Probe on PC_OUTPUT
  // Probe on AC_OUTPUT
  // Probe on AR_OUTPUT
  // Probe on IR_OUTPUT
  and and_4 (and_4_out, D0, T5);
  and and_5 (and_5_out, D2, T5);
  and and_6 (and_6_out, D1, T5);
  SC_CLR_LOGIC sc_clr_logic_1 (
    .R(1'b0), .T2(T2), .D0(D0), .T5(T5), .D1(D1), .D2(D2), .D3(D3), .T4(T4), .D4(D4), .D5(D5), .D6(D6),
    .T6(T6), .D7(D7), .T3(T3), .I(I), .SC_CLR(SC_CLR));
  BUS_SELECTION bus_selection_1 (
    .D4(D4), .T4(T4), .D5(D5), .T5(T5), .T0(T0), .D2(D2), .D6(D6), .T6(T6), .D3(D3), .T2(T2), .T1(T1),
    .R(1'b0), .D7(D7), .I(I), .T3(T3), .D1(D1), .D0(D0), .S2S1S0(BUS_S2S1S0));
  ALU_SELECTION alu_selection_1 (
    .AND_a1(and_4_out), .LOAD_DR_a3(and_5_out), .CMP_AC_a5(rB9), .ADD_a2(and_6_out), .SHL_a7(rB6),
    .SHR_a6(rB7), .INPR_a4(1'b0), .ALU_S2S1S0(ALU_S2S1S0));
  AC_DR_COMPARATOR ac_dr_comparator_1 (
    .AC_DATA(AC_OUTPUT), .DR_DATA(DR_OUTPUT), .AC_EQUAL_0(AC_IS_0), .DR_EQUAL_0(DR_IS_0), .AC_15(AC_15));
  // Probe on BUS_S2S1S0
  // Probe on ALU_S2S1S0
  MEMORY_LOGIC memory_logic_1 (
    .D3(D3), .T4(T4), .D5(D5), .D6(D6), .T6(T6), .T1(T1), .I(I), .D7(D7), .T3(T3), .D0(D0), .D1(D1), .D2(D2),
    .R(1'b0), .MEMORY_WRITE(WRITE_EN), .MEMORY_READ(READ_EN));
  AR_LOGIC ar_logic_1 (
    .D7(D7), .I(I), .T3(T3), .T2(T2), .R(1'b0), .T0(T0), .D5(D5), .T4(T4), .AR_LOAD(AR_LOAD), .AR_INR(AR_INR));
  DR_LOGIC dr_logic_1 (.D0(D0), .T4(T4), .D1(D1), .D2(D2), .D6(D6), .T5(T5), .DR_LOAD(DR_LOAD), .DR_INR(DR_INR));
  AC_LOGIC ac_logic_1 (
    .D0(D0), .T5(T5), .D1(D1), .D2(D2), .rB9(rB9), .rB7(rB7), .rB6(rB6), .rB5(rB5), .rB11(rB11),
    .AC_LOAD(AC_LOAD), .AC_INR(AC_INR), .AC_CLR(AC_CLR));
  PC_LOGIC pc_logic_1 (
    .T1(T1), .DR_IS_0(DR_IS_0), .R(1'b0), .D6(D6), .T6(T6), .rB4(rB4), .AC_15(AC_15), .rB3(rB3),
    .E_IS_0(E_output), .rB1(rB1), .AC_IS_0(AC_IS_0), .rB2(rB2), .D4(D4), .T4(T4), .D5(D5), .T5(T5),
    .PC_CLR(PC_CLR), .PC_INR(PC_INR), .PC_LOAD(PC_LOAD));
  IR_LOGIC ir_logic_1 (.R(1'b0), .T1(T1), .IR_LOAD(IR_LOAD));

  // Other names for the same wires on the sheet: clr = in_2
endmodule

module SEQUENCE_COUNTER (
  input  SC_INR,
  input  SC_CLR,
  input  SC_CLK,
  output [7:0] T0_15
);

  wire [2:0] adder_1_out, multiplexer_1_out, multiplexer_2_out, register_1_q;

  Adder #(.width(3)) adder_1 (.a(register_1_q), .b(3'b001), .out(adder_1_out), .cin(1'b0));  // open: cout
  Multiplexer #(.width(3)) multiplexer_1 (.in0(register_1_q), .in1(adder_1_out), .out(multiplexer_1_out), .sel(SC_INR));
  Register #(.width(3)) register_1 (.D(multiplexer_2_out), .clk(SC_CLK), .Q(register_1_q));  // open: en, clr
  Multiplexer #(.width(3)) multiplexer_2 (.in0(multiplexer_1_out), .in1(3'b000), .out(multiplexer_2_out), .sel(SC_CLR));
  Decoder #(.enable("false"), .select(3)) decoder_1 (
    .out0(T0_15[0]), .out1(T0_15[1]), .out2(T0_15[2]), .out3(T0_15[3]), .out4(T0_15[4]), .out5(T0_15[5]),
    .out6(T0_15[6]), .out7(T0_15[7]), .sel(register_1_q));
endmodule

module INSTRUCTION_REGISTER (
  input  [15:0] IR_15_0_BITS,
  input  SC_INR,
  input  SC_CLR,
  input  SC_CLK,
  input  Ibit_Control,
  input  CLK,
  output rB0,
  output rB1,
  output rB2,
  output D0,
  output D1,
  output D2,
  output rB3,
  output D3,
  output rB4,
  output rB5,
  output T0,
  output D4,
  output T1,
  output T2,
  output D5,
  output T3,
  output rB6,
  output D6,
  output D7,
  output rB7,
  output rB8,
  output T4,
  output rB9,
  output T5,
  output T6,
  output rB10,
  output T7,
  output rB11,
  output I
);

  wire multiplexer_1_out, not_1_out, r;

  SEQUENCE_COUNTER sequence_counter_1 (
    .SC_INR(SC_INR), .SC_CLR(SC_CLR), .SC_CLK(SC_CLK), .T0_15({T7, T6, T5, T4, T3, T2, T1, T0}));
  Multiplexer #(.enable("true")) multiplexer_1 (
    .in0(I), .in1(IR_15_0_BITS[15]), .out(multiplexer_1_out), .sel(Ibit_Control));  // open: en
  D_Flip_Flop d_ff_1 (.D(multiplexer_1_out), .clk(CLK), .Q(I));  // open: Qn, preset, reset
  Decoder #(.enable("false"), .select(3)) decoder_1 (
    .out0(D0), .out1(D1), .out2(D2), .out3(D3), .out4(D4), .out5(D5), .out6(D6), .out7(D7),
    .sel(IR_15_0_BITS[14:12]));
  not not_1 (not_1_out, I);
  and and_1 (r, D7, not_1_out, T3);
  and and_2 (rB0, r, IR_15_0_BITS[0]);
  and and_3 (rB1, r, IR_15_0_BITS[1]);
  and and_4 (rB2, r, IR_15_0_BITS[2]);
  and and_5 (rB3, r, IR_15_0_BITS[3]);
  and and_6 (rB4, r, IR_15_0_BITS[4]);
  and and_7 (rB5, r, IR_15_0_BITS[5]);
  and and_8 (rB6, r, IR_15_0_BITS[6]);
  and and_9 (rB7, r, IR_15_0_BITS[7]);
  and and_10 (rB8, r, IR_15_0_BITS[8]);
  and and_11 (rB9, r, IR_15_0_BITS[9]);
  and and_12 (rB10, r, IR_15_0_BITS[10]);
  and and_13 (rB11, r, IR_15_0_BITS[11]);

  // Other names for the same wires on the sheet: B0 = IR_15_0_BITS[0]; B1 = IR_15_0_BITS[1]; B2 = IR_15_0_BITS[2];
  //   B3 = IR_15_0_BITS[3]; B4 = IR_15_0_BITS[4]; B5 = IR_15_0_BITS[5]; B6 = IR_15_0_BITS[6]; B7 = IR_15_0_BITS[7];
  //   B8 = IR_15_0_BITS[8]; B9 = IR_15_0_BITS[9]; B10 = IR_15_0_BITS[10]; B11 = IR_15_0_BITS[11]
endmodule

module MEMORY_LOGIC (
  input  D3,
  input  T4,
  input  D5,
  input  D6,
  input  T6,
  input  T1,
  input  I,
  input  D7,
  input  T3,
  input  D0,
  input  D1,
  input  D2,
  input  R,
  output MEMORY_WRITE,
  output MEMORY_READ
);

  wire and_1_out, and_2_out, and_3_out, and_4_out, and_5_out, and_6_out, not_1_out, not_2_out, or_1_out;

  and and_1 (and_1_out, D3, T4);
  and and_2 (and_2_out, T4, D5);
  and and_3 (and_3_out, D6, T6);
  not not_1 (not_1_out, D7);
  and and_4 (and_4_out, T1, not_2_out);
  and and_5 (and_5_out, I, not_1_out, T3);
  or or_1 (or_1_out, D0, D1, D2, D6);
  or or_2 (MEMORY_WRITE, and_1_out, and_2_out, and_3_out);
  and and_6 (and_6_out, or_1_out, T4);
  or or_3 (MEMORY_READ, and_4_out, and_5_out, and_6_out);
  not not_2 (not_2_out, R);
endmodule

module IR_LOGIC (
  input  R,
  input  T1,
  output IR_LOAD
);

  wire not_1_out;

  not not_1 (not_1_out, R);
  and and_1 (IR_LOAD, not_1_out, T1);
endmodule

module E_FLIFLOP (
  input  C_out,
  input  AC_0,
  input  AC_15,
  input  E_COM,
  input  D1T5,
  input  CLK,
  input  rB6,
  input  E_LOAD,
  input  rB7,
  input  E_CLR,
  output E_EXTENDED_BIT_OUTPUT
);

  wire E_IP, multiplexer_1_out, multiplexer_2_out, multiplexer_3_out, not_1_out, or_1_out;
  wire [1:0] S1S0;

  not not_1 (not_1_out, E_EXTENDED_BIT_OUTPUT);
  Multiplexer multiplexer_1 (.in0(E_EXTENDED_BIT_OUTPUT), .in1(not_1_out), .out(multiplexer_1_out), .sel(E_COM));
  Multiplexer multiplexer_2 (.in0(multiplexer_1_out), .in1(E_IP), .out(multiplexer_2_out), .sel(or_1_out));
  or or_1 (or_1_out, D1T5, rB6, rB7);
  D_Flip_Flop d_ff_1 (.D(multiplexer_3_out), .clk(CLK), .Q(E_EXTENDED_BIT_OUTPUT));  // open: Qn, preset, reset
  Multiplexer multiplexer_3 (.in0(multiplexer_2_out), .in1(1'b0), .out(multiplexer_3_out), .sel(E_CLR));
  or or_2 (S1S0[0], D1T5, rB6);
  or or_3 (S1S0[1], rB6, rB7);
  Multiplexer #(.select(2)) multiplexer_4 (.in0(1'b0), .in1(C_out), .in2(AC_0), .in3(AC_15), .out(E_IP), .sel(S1S0));
endmodule

module IR (
  input  [15:0] DATA_IN,
  input  LOAD_IR,
  input  CLK,
  output [15:0] DATA_OUT
);

  wire [15:0] multiplexer_1_out;

  Multiplexer #(.width(16)) multiplexer_1 (.in0(DATA_OUT), .in1(DATA_IN), .out(multiplexer_1_out), .sel(LOAD_IR));
  Register #(.width(16)) register_1 (.D(multiplexer_1_out), .clk(CLK), .Q(DATA_OUT));  // open: en, clr
endmodule

module ADDRESS_REGISTER (
  input  AR_INR,
  input  AR_LOAD,
  input  CLK,
  input  AR_CLR,
  input  [15:0] DATA_IN,
  output [11:0] ADDRESS,
  output [15:0] DATA_OUT
);

  wire [11:0] adder_1_out, multiplexer_1_out, multiplexer_2_out, multiplexer_3_out;

  Adder #(.width(12)) adder_1 (.a(ADDRESS), .b(12'h1), .out(adder_1_out));  // open: cin, cout
  Multiplexer #(.width(12)) multiplexer_1 (.in0(ADDRESS), .in1(adder_1_out), .out(multiplexer_1_out), .sel(AR_INR));
  Multiplexer #(.width(12)) multiplexer_2 (
    .in0(multiplexer_1_out), .in1(DATA_IN[11:0]), .out(multiplexer_2_out), .sel(AR_LOAD));
  Multiplexer #(.width(12)) multiplexer_3 (
    .in0(multiplexer_2_out), .in1({12{1'b0}}), .out(multiplexer_3_out), .sel(AR_CLR));
  Register #(.width(12)) register_1 (.D(multiplexer_3_out), .clk(CLK), .Q(ADDRESS));  // open: en, clr

  assign DATA_OUT = {4'b0000, ADDRESS};
endmodule

module PROGRAM_COUNTER (
  input  PC_INR,
  input  PC_LOAD,
  input  CLK,
  input  PC_CLR,
  input  [15:0] DATA_IN,
  output [15:0] DATA_OUT
);

  wire [11:0] adder_1_out, multiplexer_1_out, multiplexer_2_out, multiplexer_3_out;

  Adder #(.width(12)) adder_1 (.a(DATA_OUT[11:0]), .b(12'h1), .out(adder_1_out));  // open: cin, cout
  Multiplexer #(.width(12)) multiplexer_1 (
    .in0(DATA_OUT[11:0]), .in1(adder_1_out), .out(multiplexer_1_out), .sel(PC_INR));
  Multiplexer #(.width(12)) multiplexer_2 (
    .in0(multiplexer_1_out), .in1(DATA_IN[11:0]), .out(multiplexer_2_out), .sel(PC_LOAD));
  Multiplexer #(.width(12)) multiplexer_3 (
    .in0(multiplexer_2_out), .in1({12{1'b0}}), .out(multiplexer_3_out), .sel(PC_CLR));
  Register #(.width(12)) register_1 (.D(multiplexer_3_out), .clk(CLK), .Q(DATA_OUT[11:0]));  // open: en, clr

  assign DATA_OUT[15:12] = 4'b0000;
endmodule

module DATA_REGISTER (
  input  DATA_INR,
  input  [15:0] DATA_IN,
  input  CLK,
  input  DATA_LOAD,
  input  DATA_CLR,
  output [15:0] DATA_OUT
);

  wire [15:0] adder_1_out, multiplexer_1_out, multiplexer_2_out, multiplexer_3_out;

  Adder #(.width(16)) adder_1 (.a(DATA_OUT), .b(16'h1), .out(adder_1_out));  // open: cin, cout
  Multiplexer #(.width(16)) multiplexer_1 (.in0(DATA_OUT), .in1(adder_1_out), .out(multiplexer_1_out), .sel(DATA_INR));
  Multiplexer #(.width(16)) multiplexer_2 (
    .in0(multiplexer_1_out), .in1(DATA_IN), .out(multiplexer_2_out), .sel(DATA_LOAD));
  Multiplexer #(.width(16)) multiplexer_3 (
    .in0(multiplexer_2_out), .in1({16{1'b0}}), .out(multiplexer_3_out), .sel(DATA_CLR));
  Register #(.width(16)) register_1 (.D(multiplexer_3_out), .clk(CLK), .Q(DATA_OUT));  // open: en, clr
endmodule

module TEMPORARY_REGISTER (
  input  TR_INR,
  input  [15:0] DATA_IN,
  input  CLK,
  input  TR_LOAD,
  input  TR_CLR,
  output [15:0] DATA_OUT
);

  wire [15:0] adder_1_out, multiplexer_1_out, multiplexer_2_out, multiplexer_3_out;

  Adder #(.width(16)) adder_1 (.a(DATA_OUT), .b(16'h1), .out(adder_1_out));  // open: cin, cout
  Multiplexer #(.width(16)) multiplexer_1 (.in0(DATA_OUT), .in1(adder_1_out), .out(multiplexer_1_out), .sel(TR_INR));
  Multiplexer #(.width(16)) multiplexer_2 (
    .in0(multiplexer_1_out), .in1(DATA_IN), .out(multiplexer_2_out), .sel(TR_LOAD));
  Multiplexer #(.width(16)) multiplexer_3 (
    .in0(multiplexer_2_out), .in1({16{1'b0}}), .out(multiplexer_3_out), .sel(TR_CLR));
  Register #(.width(16)) register_1 (.D(multiplexer_3_out), .clk(CLK), .Q(DATA_OUT));  // open: en, clr
endmodule

module ACCUMULATOR (
  input  AC_INR,
  input  [15:0] DATA_IN,
  input  CLK,
  input  AC_LOAD,
  input  AC_CLR,
  output [15:0] DATA_OUT
);

  wire [15:0] adder_1_out, multiplexer_1_out, multiplexer_2_out, multiplexer_3_out;

  Adder #(.width(16)) adder_1 (.a(DATA_OUT), .b(16'h1), .out(adder_1_out));  // open: cin, cout
  Multiplexer #(.width(16)) multiplexer_1 (.in0(DATA_OUT), .in1(adder_1_out), .out(multiplexer_1_out), .sel(AC_INR));
  Multiplexer #(.width(16)) multiplexer_2 (
    .in0(multiplexer_1_out), .in1(DATA_IN), .out(multiplexer_2_out), .sel(AC_LOAD));
  Multiplexer #(.width(16)) multiplexer_3 (
    .in0(multiplexer_2_out), .in1({16{1'b0}}), .out(multiplexer_3_out), .sel(AC_CLR));
  Register #(.width(16)) register_1 (.D(multiplexer_3_out), .clk(CLK), .Q(DATA_OUT));  // open: en, clr
endmodule

module ALU (
  input  [15:0] DataRegister,
  input  [15:0] Accumulator,
  input  [15:0] INPR,
  input  [2:0] ALU_SelectionBits,
  input  IR,
  input  IL,
  output Cout,
  output [15:0] ALU_RESULT
);

  wire [15:0] adder_1_out, and_1_out, not_1_out;

  assign not_1_out = ~Accumulator;  // NOT_Gate not_1, 16 bits wide
  assign and_1_out = Accumulator & DataRegister;  // AND_Gate and_1, 16 bits wide
  Adder #(.width(16)) adder_1 (.a(Accumulator), .b(DataRegister), .out(adder_1_out), .cin(1'b0), .cout(Cout));
  Multiplexer #(.select(3), .width(16)) multiplexer_1 (
    .in1(and_1_out), .in2(adder_1_out), .in3(DataRegister), .in4(INPR), .in5(not_1_out),
    .in6({IR, Accumulator[15:1]}), .in7({Accumulator[14:0], IL}), .out(ALU_RESULT), .sel(ALU_SelectionBits));  // open: in0
endmodule

module COMMON_BUS (
  input  E_COMP,
  input  READ_ENABLE,
  input  E_LOAD,
  input  E_CLR,
  input  WRITE_ENABLE,
  input  [2:0] ALU_SELECTION_BITS,
  input  CLK,
  input  [2:0] CommonBus_Selection,
  input  AR_INR,
  input  AR_LOAD,
  input  AR_CLR,
  input  PC_INR,
  input  PC_LOAD,
  input  PC_CLR,
  input  DATA_INR,
  input  DATA_LOAD,
  input  DATA_CLR,
  input  AC_INR,
  input  AC_LOAD,
  input  AC_CLR,
  input  IR_LOAD,
  input  TR_INR,
  input  TR_LOAD,
  input  TR_CLR,
  input  rB7,
  input  rB6,
  input  D1T5,
  output E_output,
  output [15:0] AR_out,
  output [15:0] PC_out,
  output [15:0] DR_15_0,
  output [15:0] AC_15_0,
  output [15:0] IR_DATA
);

  wire Cout;
  wire [11:0] address_register_1_address;
  wire [15:0] ALU_Output, MEMUnit_dout, multiplexer_1_out, temporary_register_1_data_out;

  E_FLIFLOP e_fliflop_1 (
    .C_out(Cout), .AC_0(AC_15_0[0]), .AC_15(AC_15_0[15]), .E_COM(E_COMP), .D1T5(D1T5), .CLK(CLK), .rB6(rB6),
    .E_LOAD(E_LOAD), .rB7(rB7), .E_CLR(E_CLR), .E_EXTENDED_BIT_OUTPUT(E_output));
  RAM #(.addrWidth(12), .asyncread("true"), .dataWidth(16)) MEMUnit (
    .addr(address_register_1_address), .we(WRITE_ENABLE), .oe(READ_ENABLE), .clk(CLK),
    .din(multiplexer_1_out), .dout(MEMUnit_dout));
  ADDRESS_REGISTER address_register_1 (
    .AR_INR(AR_INR), .AR_LOAD(AR_LOAD), .CLK(CLK), .AR_CLR(AR_CLR), .DATA_IN(multiplexer_1_out),
    .ADDRESS(address_register_1_address), .DATA_OUT(AR_out));
  PROGRAM_COUNTER program_counter_1 (
    .PC_INR(PC_INR), .PC_LOAD(PC_LOAD), .CLK(CLK), .PC_CLR(PC_CLR), .DATA_IN(multiplexer_1_out),
    .DATA_OUT(PC_out));
  DATA_REGISTER data_register_1 (
    .DATA_INR(DATA_INR), .DATA_IN(multiplexer_1_out), .CLK(CLK), .DATA_LOAD(DATA_LOAD), .DATA_CLR(DATA_CLR),
    .DATA_OUT(DR_15_0));
  ACCUMULATOR accumulator_1 (
    .AC_INR(AC_INR), .DATA_IN(ALU_Output), .CLK(CLK), .AC_LOAD(AC_LOAD), .AC_CLR(AC_CLR), .DATA_OUT(AC_15_0));
  IR ir_1 (.DATA_IN(multiplexer_1_out), .LOAD_IR(IR_LOAD), .CLK(CLK), .DATA_OUT(IR_DATA));
  TEMPORARY_REGISTER temporary_register_1 (
    .TR_INR(TR_INR), .DATA_IN(multiplexer_1_out), .CLK(CLK), .TR_LOAD(TR_LOAD), .TR_CLR(TR_CLR),
    .DATA_OUT(temporary_register_1_data_out));
  Multiplexer #(.select(3), .width(16)) multiplexer_1 (
    .in1(AR_out), .in2(PC_out), .in3(DR_15_0), .in4(AC_15_0), .in5(IR_DATA),
    .in6(temporary_register_1_data_out), .in7(MEMUnit_dout), .out(multiplexer_1_out),
    .sel(CommonBus_Selection));  // open: in0
  ALU alu_1 (
    .DataRegister(DR_15_0), .Accumulator(AC_15_0), .ALU_SelectionBits(ALU_SELECTION_BITS), .IR(E_output),
    .IL(E_output), .Cout(Cout), .ALU_RESULT(ALU_Output));  // open: INPR

  // Other names for the same wires on the sheet: AC_0 = AC_15_0[0]; AC_DATA[15:0] = AC_15_0; AC_15 = AC_15_0[15];
  //   DR_DATA[15:0] = DR_15_0; E_out = E_output
endmodule

module AR_LOGIC (
  input  D7,
  input  I,
  input  T3,
  input  T2,
  input  R,
  input  T0,
  input  D5,
  input  T4,
  output AR_LOAD,
  output AR_INR
);

  wire and_1_out, and_2_out, and_3_out, not_1_out, not_2_out;

  not not_1 (not_1_out, D7);
  not not_2 (not_2_out, R);
  and and_1 (and_1_out, not_1_out, I, T3);
  and and_2 (and_2_out, T2, not_2_out);
  and and_3 (and_3_out, not_2_out, T0);
  and and_4 (AR_INR, D5, T4);
  or or_1 (AR_LOAD, and_1_out, and_2_out, and_3_out);
endmodule

module DR_LOGIC (
  input  D0,
  input  T4,
  input  D1,
  input  D2,
  input  D6,
  input  T5,
  output DR_LOAD,
  output DR_INR
);

  wire and_1_out, and_2_out, and_3_out, and_4_out;

  and and_1 (and_1_out, D0, T4);
  and and_2 (and_2_out, T4, D1);
  and and_3 (and_3_out, T4, D2);
  and and_4 (and_4_out, T4, D6);
  and and_5 (DR_INR, D6, T5);
  or or_1 (DR_LOAD, and_1_out, and_2_out, and_3_out, and_4_out);
endmodule

module BUS_SELECTION (
  input  D4,
  input  T4,
  input  D5,
  input  T5,
  input  T0,
  input  D2,
  input  D6,
  input  T6,
  input  D3,
  input  T2,
  input  T1,
  input  R,
  input  D7,
  input  I,
  input  T3,
  input  D1,
  input  D0,
  output [2:0] S2S1S0
);

  wire and_1_out, and_2_out, and_3_out, and_4_out, and_5_out, and_6_out, and_7_out, and_8_out, and_9_out,
       and_10_out, not_1_out, not_2_out, not_3_out, or_1_out, x1, x2, x3, x4, x5, x6, x7;

  or or_1 (or_1_out, D2, D6, D1, D0);
  not not_1 (not_1_out, R);
  not not_2 (not_2_out, R);
  not not_3 (not_3_out, D7);
  and and_1 (and_1_out, not_1_out, T0);
  and and_2 (and_2_out, T1, not_2_out);
  and and_3 (and_3_out, not_3_out, I, T3);
  and and_4 (and_4_out, or_1_out, T4);
  and and_5 (and_5_out, D4, T4);
  and and_6 (and_6_out, D5, T5);
  and and_7 (and_7_out, T4, D5);
  and and_8 (and_8_out, T5, D2);
  and and_9 (and_9_out, D6, T6);
  and and_10 (and_10_out, T4, D3);
  and and_11 (x6, T1, R);
  and and_12 (x5, not_1_out, T2);
  or or_2 (x1, and_5_out, and_6_out);
  or or_3 (x2, and_7_out, and_1_out);
  or or_4 (x3, and_8_out, and_9_out);
  or or_5 (x4, and_10_out, 1'b0);
  or or_6 (x7, and_3_out, and_2_out, and_4_out);
  or or_7 (S2S1S0[0], x1, x3, x5, x7);
  or or_8 (S2S1S0[1], x2, x3, x6, x7);
  or or_9 (S2S1S0[2], x4, x5, x6, x7);

  // Notes on the sheet:
  //   AR
  //   PC
  //   DR
  //   AC
  //   IR
  //   TR
  //   Memory
  //   S0
  //   S1
  //   S2
endmodule

module AC_DR_COMPARATOR (
  input  [15:0] AC_DATA,
  input  [15:0] DR_DATA,
  output AC_EQUAL_0,
  output DR_EQUAL_0,
  output AC_15
);

  Comparator #(.width(16)) comparator_1 (.a({16{1'b0}}), .b(AC_DATA), .eq(AC_EQUAL_0));  // open: gt, lt
  Comparator #(.width(16)) comparator_2 (.a({16{1'b0}}), .b(DR_DATA), .eq(DR_EQUAL_0));  // open: gt, lt

  assign AC_15 = AC_DATA[15];
endmodule

module ALU_SELECTION (
  input  AND_a1,
  input  LOAD_DR_a3,
  input  CMP_AC_a5,
  input  ADD_a2,
  input  SHL_a7,
  input  SHR_a6,
  input  INPR_a4,
  output [2:0] ALU_S2S1S0
);

  or or_1 (ALU_S2S1S0[0], AND_a1, LOAD_DR_a3, CMP_AC_a5, SHL_a7);
  or or_2 (ALU_S2S1S0[1], ADD_a2, LOAD_DR_a3, SHL_a7, SHR_a6);
  or or_3 (ALU_S2S1S0[2], SHL_a7, SHR_a6, CMP_AC_a5, INPR_a4);
endmodule

module PC_LOGIC (
  input  T1,
  input  DR_IS_0,
  input  R,
  input  D6,
  input  T6,
  input  rB4,
  input  AC_15,
  input  rB3,
  input  E_IS_0,
  input  rB1,
  input  AC_IS_0,
  input  rB2,
  input  D4,
  input  T4,
  input  D5,
  input  T5,
  output PC_CLR,
  output PC_INR,
  output PC_LOAD
);

  wire and_1_out, and_2_out, and_3_out, and_4_out, and_5_out, and_6_out, and_7_out, and_8_out, and_9_out,
       not_1_out, not_2_out, not_3_out;

  not not_1 (not_1_out, AC_15);
  not not_2 (not_2_out, E_IS_0);
  and and_1 (and_1_out, D6, T6);
  and and_2 (and_2_out, rB4, not_1_out);
  and and_3 (and_3_out, AC_15, rB3);
  and and_4 (and_4_out, not_2_out, rB1);
  and and_5 (and_5_out, AC_IS_0, rB2);
  and and_6 (and_6_out, D4, T4);
  and and_7 (and_7_out, D5, T5);
  and and_8 (and_8_out, DR_IS_0, and_1_out);
  or or_1 (PC_LOAD, and_6_out, and_7_out);
  not not_3 (not_3_out, R);
  or or_2 (PC_INR, and_9_out, and_8_out, and_2_out, and_3_out, and_4_out, and_5_out);
  and and_9 (and_9_out, not_3_out, T1);
  and and_10 (PC_CLR, T1, R);
endmodule

module SC_CLR_LOGIC (
  input  R,
  input  T2,
  input  D0,
  input  T5,
  input  D1,
  input  D2,
  input  D3,
  input  T4,
  input  D4,
  input  D5,
  input  D6,
  input  T6,
  input  D7,
  input  T3,
  input  I,
  output SC_CLR
);

  wire and_1_out, and_2_out, and_3_out, and_4_out, and_5_out, and_6_out, and_7_out, and_8_out, and_9_out,
       not_1_out;

  not not_1 (not_1_out, I);
  and and_1 (and_1_out, R, T2);
  and and_2 (and_2_out, D0, T5);
  and and_3 (and_3_out, T5, D1);
  and and_4 (and_4_out, T5, D2);
  and and_5 (and_5_out, D3, T4);
  and and_6 (and_6_out, T4, D4);
  and and_7 (and_7_out, T5, D5);
  and and_8 (and_8_out, D6, T6);
  and and_9 (and_9_out, D7, not_1_out, T3);
  or or_1 (SC_CLR, and_1_out, and_2_out, and_3_out, and_4_out, and_5_out, and_6_out, and_7_out, and_8_out, and_9_out);

  // Notes on the sheet:
  //   Interrupt
  //   AND
  //   ADD
  //   LOAD
  //   STORE
  //   BUN
  //   LOAD
  //   ISZ
endmodule

module AC_LOGIC (
  input  D0,
  input  T5,
  input  D1,
  input  D2,
  input  rB9,
  input  rB7,
  input  rB6,
  input  rB5,
  input  rB11,
  output AC_LOAD,
  output AC_INR,
  output AC_CLR
);

  wire and_1_out, and_2_out, and_3_out;

  and and_1 (and_1_out, D0, T5);
  and and_2 (and_2_out, T5, D1);
  and and_3 (and_3_out, T5, D2);
  or or_1 (AC_LOAD, and_1_out, and_2_out, and_3_out, rB9, rB7, rB6);

  assign AC_CLR = rB11;
  assign AC_INR = rB5;
endmodule
